// Logisim project Cartesian_Game.circ as structural Verilog: 24 circuits, main circuit main
module main (
  output [3:0] out_1,
  output [3:0] out_2
);

  wire eixo_x_dezenas_1_out_2, eixo_x_dezenas_1_out_3, eixo_x_unidades_1_a, eixo_x_unidades_1_b,
       eixo_x_unidades_1_c, eixo_x_unidades_1_d, eixo_x_unidades_1_e, eixo_x_unidades_1_f,
       eixo_x_unidades_1_g, eixo_y_dezenas_1_out_2, eixo_y_dezenas_1_out_3, eixo_y_unidades_1_a,
       eixo_y_unidades_1_b, eixo_y_unidades_1_c, eixo_y_unidades_1_d, eixo_y_unidades_1_e,
       eixo_y_unidades_1_f, eixo_y_unidades_1_g;
  wire [14:0] eixos_1_out_3, eixos_1_out_4, eixos_1_out_5, eixos_1_out_6, eixos_1_out_7, eixos_1_out_8,
       eixos_1_out_9, eixos_1_out_10, eixos_1_out_11, eixos_1_out_12, eixos_1_out_13, eixos_1_out_14,
       eixos_1_out_15, eixos_1_out_16, eixos_1_out_17;

  DotMatrix #(.matrixcols(15), .matrixrows(15)) dotmatrix_1 (
    .col0(eixos_1_out_3), .col1(eixos_1_out_4), .col2(eixos_1_out_5), .col3(eixos_1_out_6),
    .col4(eixos_1_out_7), .col5(eixos_1_out_8), .col6(eixos_1_out_9), .col7(eixos_1_out_10),
    .col8(eixos_1_out_11), .col9(eixos_1_out_12), .col10(eixos_1_out_13), .col11(eixos_1_out_14),
    .col12(eixos_1_out_15), .col13(eixos_1_out_16), .col14(eixos_1_out_17));
  Eixos eixos_1 (
    .out_3(eixos_1_out_3), .out_4(eixos_1_out_4), .out_5(eixos_1_out_5), .out_6(eixos_1_out_6),
    .out_7(eixos_1_out_7), .out_8(eixos_1_out_8), .out_9(eixos_1_out_9), .out_10(eixos_1_out_10),
    .out_11(eixos_1_out_11), .out_12(eixos_1_out_12), .out_13(eixos_1_out_13), .out_14(eixos_1_out_14),
    .out_15(eixos_1_out_15), .out_16(eixos_1_out_16), .out_17(eixos_1_out_17), .in_2(out_2), .in_1(out_1));
  Joystick joystick_1 (.x(out_1), .y(out_2));
  _7_Segment_Display u_7_segment_display_1 (
    .f(eixo_y_dezenas_1_out_2), .a(eixo_y_dezenas_1_out_2), .b(eixo_y_dezenas_1_out_3),
    .e(eixo_y_dezenas_1_out_2), .d(eixo_y_dezenas_1_out_2), .c(eixo_y_dezenas_1_out_3));  // open: g, dp
  Eixo_Y_Dezenas eixo_y_dezenas_1 (.out_2(eixo_y_dezenas_1_out_2), .out_3(eixo_y_dezenas_1_out_3), .in_1(out_2));
  _7_Segment_Display u_7_segment_display_2 (
    .g(eixo_y_unidades_1_g), .f(eixo_y_unidades_1_a), .a(eixo_y_unidades_1_b), .b(eixo_y_unidades_1_c),
    .e(eixo_y_unidades_1_f), .d(eixo_y_unidades_1_e), .c(eixo_y_unidades_1_d));  // open: dp
  Eixo_Y_Unidades eixo_y_unidades_1 (
    .G(eixo_y_unidades_1_g), .A(eixo_y_unidades_1_a), .B(eixo_y_unidades_1_b), .C(eixo_y_unidades_1_c),
    .D(eixo_y_unidades_1_d), .E(eixo_y_unidades_1_e), .F(eixo_y_unidades_1_f), .in_1(out_2));
  _7_Segment_Display u_7_segment_display_3 (
    .f(eixo_x_dezenas_1_out_2), .a(eixo_x_dezenas_1_out_2), .b(eixo_x_dezenas_1_out_3),
    .e(eixo_x_dezenas_1_out_2), .d(eixo_x_dezenas_1_out_2), .c(eixo_x_dezenas_1_out_3));  // open: g, dp
  Eixo_X_Dezenas eixo_x_dezenas_1 (.out_2(eixo_x_dezenas_1_out_2), .out_3(eixo_x_dezenas_1_out_3), .in_1(out_1));
  Eixo_X_Unidades eixo_x_unidades_1 (
    .G(eixo_x_unidades_1_g), .A(eixo_x_unidades_1_a), .B(eixo_x_unidades_1_b), .C(eixo_x_unidades_1_c),
    .D(eixo_x_unidades_1_d), .E(eixo_x_unidades_1_e), .F(eixo_x_unidades_1_f), .in_1(out_1));
  _7_Segment_Display u_7_segment_display_4 (
    .g(eixo_x_unidades_1_g), .f(eixo_x_unidades_1_a), .a(eixo_x_unidades_1_b), .b(eixo_x_unidades_1_c),
    .e(eixo_x_unidades_1_f), .d(eixo_x_unidades_1_e), .c(eixo_x_unidades_1_d));  // open: dp

  // Notes on the sheet:
  //   Eixo Y
  //   Eixo X
endmodule

module Eixos (
  input  [3:0] in_1,
  input  [3:0] in_2,
  output [14:0] out_3,
  output [14:0] out_4,
  output [14:0] out_5,
  output [14:0] out_6,
  output [14:0] out_7,
  output [14:0] out_8,
  output [14:0] out_9,
  output [14:0] out_10,
  output [14:0] out_11,
  output [14:0] out_12,
  output [14:0] out_13,
  output [14:0] out_14,
  output [14:0] out_15,
  output [14:0] out_16,
  output [14:0] out_17
);

  wire [14:0] Demux_Y_out_20;

  Demux_Y Demux_Y (
    .in_1(1'b1), .in_2(in_2[3]), .in_3(in_2[2]), .in_4(in_2[1]), .in_5(in_2[0]), .out_6(Demux_Y_out_20[14]),
    .out_7(Demux_Y_out_20[13]), .out_8(Demux_Y_out_20[12]), .out_9(Demux_Y_out_20[11]),
    .out_10(Demux_Y_out_20[10]), .out_11(Demux_Y_out_20[9]), .out_12(Demux_Y_out_20[8]),
    .out_13(Demux_Y_out_20[7]), .out_14(Demux_Y_out_20[6]), .out_15(Demux_Y_out_20[5]),
    .out_16(Demux_Y_out_20[4]), .out_17(Demux_Y_out_20[3]), .out_18(Demux_Y_out_20[2]),
    .out_19(Demux_Y_out_20[1]), .out_20(Demux_Y_out_20[0]));
  Demux_X Demux_X (
    .out_3(out_3), .out_4(out_4), .out_5(out_5), .out_6(out_6), .out_7(out_7), .out_8(out_8), .out_9(out_9),
    .out_10(out_10), .out_11(out_11), .out_12(out_12), .out_13(out_13), .out_14(out_14), .out_15(out_15),
    .out_16(out_16), .out_17(out_17), .in_2(Demux_Y_out_20), .in_1(in_1));
endmodule

module Demux_X (
  input  [3:0] in_1,
  input  [14:0] in_2,
  output [14:0] out_3,
  output [14:0] out_4,
  output [14:0] out_5,
  output [14:0] out_6,
  output [14:0] out_7,
  output [14:0] out_8,
  output [14:0] out_9,
  output [14:0] out_10,
  output [14:0] out_11,
  output [14:0] out_12,
  output [14:0] out_13,
  output [14:0] out_14,
  output [14:0] out_15,
  output [14:0] out_16,
  output [14:0] out_17
);

  Demux_Y demux_y_1 (
    .in_1(in_2[0]), .in_2(in_1[3]), .in_3(in_1[2]), .in_4(in_1[1]), .in_5(in_1[0]), .out_6(out_3[0]),
    .out_7(out_4[0]), .out_8(out_5[0]), .out_9(out_6[0]), .out_10(out_7[0]), .out_11(out_8[0]),
    .out_12(out_9[0]), .out_13(out_10[0]), .out_14(out_11[0]), .out_15(out_12[0]), .out_16(out_13[0]),
    .out_17(out_14[0]), .out_18(out_15[0]), .out_19(out_16[0]), .out_20(out_17[0]));
  Demux_Y demux_y_2 (
    .in_1(in_2[1]), .in_2(in_1[3]), .in_3(in_1[2]), .in_4(in_1[1]), .in_5(in_1[0]), .out_6(out_3[1]),
    .out_7(out_4[1]), .out_8(out_5[1]), .out_9(out_6[1]), .out_10(out_7[1]), .out_11(out_8[1]),
    .out_12(out_9[1]), .out_13(out_10[1]), .out_14(out_11[1]), .out_15(out_12[1]), .out_16(out_13[1]),
    .out_17(out_14[1]), .out_18(out_15[1]), .out_19(out_16[1]), .out_20(out_17[1]));
  Demux_Y demux_y_3 (
    .in_1(in_2[2]), .in_2(in_1[3]), .in_3(in_1[2]), .in_4(in_1[1]), .in_5(in_1[0]), .out_6(out_3[2]),
    .out_7(out_4[2]), .out_8(out_5[2]), .out_9(out_6[2]), .out_10(out_7[2]), .out_11(out_8[2]),
    .out_12(out_9[2]), .out_13(out_10[2]), .out_14(out_11[2]), .out_15(out_12[2]), .out_16(out_13[2]),
    .out_17(out_14[2]), .out_18(out_15[2]), .out_19(out_16[2]), .out_20(out_17[2]));
  Demux_Y demux_y_4 (
    .in_1(in_2[3]), .in_2(in_1[3]), .in_3(in_1[2]), .in_4(in_1[1]), .in_5(in_1[0]), .out_6(out_3[3]),
    .out_7(out_4[3]), .out_8(out_5[3]), .out_9(out_6[3]), .out_10(out_7[3]), .out_11(out_8[3]),
    .out_12(out_9[3]), .out_13(out_10[3]), .out_14(out_11[3]), .out_15(out_12[3]), .out_16(out_13[3]),
    .out_17(out_14[3]), .out_18(out_15[3]), .out_19(out_16[3]), .out_20(out_17[3]));
  Demux_Y demux_y_5 (
    .in_1(in_2[4]), .in_2(in_1[3]), .in_3(in_1[2]), .in_4(in_1[1]), .in_5(in_1[0]), .out_6(out_3[4]),
    .out_7(out_4[4]), .out_8(out_5[4]), .out_9(out_6[4]), .out_10(out_7[4]), .out_11(out_8[4]),
    .out_12(out_9[4]), .out_13(out_10[4]), .out_14(out_11[4]), .out_15(out_12[4]), .out_16(out_13[4]),
    .out_17(out_14[4]), .out_18(out_15[4]), .out_19(out_16[4]), .out_20(out_17[4]));
  Demux_Y demux_y_6 (
    .in_1(in_2[5]), .in_2(in_1[3]), .in_3(in_1[2]), .in_4(in_1[1]), .in_5(in_1[0]), .out_6(out_3[5]),
    .out_7(out_4[5]), .out_8(out_5[5]), .out_9(out_6[5]), .out_10(out_7[5]), .out_11(out_8[5]),
    .out_12(out_9[5]), .out_13(out_10[5]), .out_14(out_11[5]), .out_15(out_12[5]), .out_16(out_13[5]),
    .out_17(out_14[5]), .out_18(out_15[5]), .out_19(out_16[5]), .out_20(out_17[5]));
  Demux_Y demux_y_7 (
    .in_1(in_2[6]), .in_2(in_1[3]), .in_3(in_1[2]), .in_4(in_1[1]), .in_5(in_1[0]), .out_6(out_3[6]),
    .out_7(out_4[6]), .out_8(out_5[6]), .out_9(out_6[6]), .out_10(out_7[6]), .out_11(out_8[6]),
    .out_12(out_9[6]), .out_13(out_10[6]), .out_14(out_11[6]), .out_15(out_12[6]), .out_16(out_13[6]),
    .out_17(out_14[6]), .out_18(out_15[6]), .out_19(out_16[6]), .out_20(out_17[6]));
  Demux_Y demux_y_8 (
    .in_1(in_2[7]), .in_2(in_1[3]), .in_3(in_1[2]), .in_4(in_1[1]), .in_5(in_1[0]), .out_6(out_3[7]),
    .out_7(out_4[7]), .out_8(out_5[7]), .out_9(out_6[7]), .out_10(out_7[7]), .out_11(out_8[7]),
    .out_12(out_9[7]), .out_13(out_10[7]), .out_14(out_11[7]), .out_15(out_12[7]), .out_16(out_13[7]),
    .out_17(out_14[7]), .out_18(out_15[7]), .out_19(out_16[7]), .out_20(out_17[7]));
  Demux_Y demux_y_9 (
    .in_1(in_2[8]), .in_2(in_1[3]), .in_3(in_1[2]), .in_4(in_1[1]), .in_5(in_1[0]), .out_6(out_3[8]),
    .out_7(out_4[8]), .out_8(out_5[8]), .out_9(out_6[8]), .out_10(out_7[8]), .out_11(out_8[8]),
    .out_12(out_9[8]), .out_13(out_10[8]), .out_14(out_11[8]), .out_15(out_12[8]), .out_16(out_13[8]),
    .out_17(out_14[8]), .out_18(out_15[8]), .out_19(out_16[8]), .out_20(out_17[8]));
  Demux_Y demux_y_10 (
    .in_1(in_2[9]), .in_2(in_1[3]), .in_3(in_1[2]), .in_4(in_1[1]), .in_5(in_1[0]), .out_6(out_3[9]),
    .out_7(out_4[9]), .out_8(out_5[9]), .out_9(out_6[9]), .out_10(out_7[9]), .out_11(out_8[9]),
    .out_12(out_9[9]), .out_13(out_10[9]), .out_14(out_11[9]), .out_15(out_12[9]), .out_16(out_13[9]),
    .out_17(out_14[9]), .out_18(out_15[9]), .out_19(out_16[9]), .out_20(out_17[9]));
  Demux_Y demux_y_11 (
    .in_1(in_2[10]), .in_2(in_1[3]), .in_3(in_1[2]), .in_4(in_1[1]), .in_5(in_1[0]), .out_6(out_3[10]),
    .out_7(out_4[10]), .out_8(out_5[10]), .out_9(out_6[10]), .out_10(out_7[10]), .out_11(out_8[10]),
    .out_12(out_9[10]), .out_13(out_10[10]), .out_14(out_11[10]), .out_15(out_12[10]), .out_16(out_13[10]),
    .out_17(out_14[10]), .out_18(out_15[10]), .out_19(out_16[10]), .out_20(out_17[10]));
  Demux_Y demux_y_12 (
    .in_1(in_2[11]), .in_2(in_1[3]), .in_3(in_1[2]), .in_4(in_1[1]), .in_5(in_1[0]), .out_6(out_3[11]),
    .out_7(out_4[11]), .out_8(out_5[11]), .out_9(out_6[11]), .out_10(out_7[11]), .out_11(out_8[11]),
    .out_12(out_9[11]), .out_13(out_10[11]), .out_14(out_11[11]), .out_15(out_12[11]), .out_16(out_13[11]),
    .out_17(out_14[11]), .out_18(out_15[11]), .out_19(out_16[11]), .out_20(out_17[11]));
  Demux_Y demux_y_13 (
    .in_1(in_2[12]), .in_2(in_1[3]), .in_3(in_1[2]), .in_4(in_1[1]), .in_5(in_1[0]), .out_6(out_3[12]),
    .out_7(out_4[12]), .out_8(out_5[12]), .out_9(out_6[12]), .out_10(out_7[12]), .out_11(out_8[12]),
    .out_12(out_9[12]), .out_13(out_10[12]), .out_14(out_11[12]), .out_15(out_12[12]), .out_16(out_13[12]),
    .out_17(out_14[12]), .out_18(out_15[12]), .out_19(out_16[12]), .out_20(out_17[12]));
  Demux_Y demux_y_14 (
    .in_1(in_2[13]), .in_2(in_1[3]), .in_3(in_1[2]), .in_4(in_1[1]), .in_5(in_1[0]), .out_6(out_3[13]),
    .out_7(out_4[13]), .out_8(out_5[13]), .out_9(out_6[13]), .out_10(out_7[13]), .out_11(out_8[13]),
    .out_12(out_9[13]), .out_13(out_10[13]), .out_14(out_11[13]), .out_15(out_12[13]), .out_16(out_13[13]),
    .out_17(out_14[13]), .out_18(out_15[13]), .out_19(out_16[13]), .out_20(out_17[13]));
  Demux_Y demux_y_15 (
    .in_1(in_2[14]), .in_2(in_1[3]), .in_3(in_1[2]), .in_4(in_1[1]), .in_5(in_1[0]), .out_6(out_3[14]),
    .out_7(out_4[14]), .out_8(out_5[14]), .out_9(out_6[14]), .out_10(out_7[14]), .out_11(out_8[14]),
    .out_12(out_9[14]), .out_13(out_10[14]), .out_14(out_11[14]), .out_15(out_12[14]), .out_16(out_13[14]),
    .out_17(out_14[14]), .out_18(out_15[14]), .out_19(out_16[14]), .out_20(out_17[14]));
endmodule

module Demux_Y (
  input  in_1,
  input  in_2,
  input  in_3,
  input  in_4,
  input  in_5,
  output out_6,
  output out_7,
  output out_8,
  output out_9,
  output out_10,
  output out_11,
  output out_12,
  output out_13,
  output out_14,
  output out_15,
  output out_16,
  output out_17,
  output out_18,
  output out_19,
  output out_20
);

  wire not_1_out, not_2_out, not_3_out, not_4_out, not_5_out, not_6_out, not_7_out, not_8_out, not_9_out,
       not_10_out, not_11_out, not_12_out, not_13_out, not_14_out, not_15_out, not_16_out, not_17_out,
       not_18_out, not_19_out, not_20_out, not_21_out, not_22_out, not_23_out, not_24_out, not_25_out,
       not_26_out, not_27_out, not_28_out;

  not not_1 (not_1_out, in_4);
  not not_2 (not_2_out, in_3);
  not not_3 (not_3_out, in_2);
  not not_4 (not_4_out, in_5);
  not not_5 (not_5_out, in_3);
  not not_6 (not_6_out, in_2);
  not not_7 (not_7_out, in_3);
  not not_8 (not_8_out, in_2);
  not not_9 (not_9_out, in_5);
  not not_10 (not_10_out, in_4);
  not not_11 (not_11_out, in_2);
  not not_12 (not_12_out, in_4);
  not not_13 (not_13_out, in_2);
  not not_14 (not_14_out, in_5);
  not not_15 (not_15_out, in_2);
  not not_16 (not_16_out, in_2);
  not not_17 (not_17_out, in_5);
  not not_18 (not_18_out, in_4);
  not not_19 (not_19_out, in_3);
  not not_20 (not_20_out, in_4);
  not not_21 (not_21_out, in_3);
  not not_22 (not_22_out, in_5);
  not not_23 (not_23_out, in_3);
  not not_24 (not_24_out, in_3);
  not not_25 (not_25_out, in_5);
  not not_26 (not_26_out, in_4);
  not not_27 (not_27_out, in_4);
  not not_28 (not_28_out, in_5);
  and and_1 (out_6, in_5, not_1_out, in_1, not_2_out, not_3_out);
  and and_2 (out_7, not_4_out, in_4, in_1, not_5_out, not_6_out);
  and and_3 (out_8, in_5, in_4, in_1, not_7_out, not_8_out);
  and and_4 (out_9, not_9_out, not_10_out, in_1, in_3, not_11_out);
  and and_5 (out_10, in_5, not_12_out, in_1, in_3, not_13_out);
  and and_6 (out_11, not_14_out, in_4, in_1, in_3, not_15_out);
  and and_7 (out_12, in_5, in_4, in_1, in_3, not_16_out);
  and and_8 (out_13, not_17_out, not_18_out, in_1, not_19_out, in_2);
  and and_9 (out_14, in_5, not_20_out, in_1, not_21_out, in_2);
  and and_10 (out_15, not_22_out, in_4, in_1, not_23_out, in_2);
  and and_11 (out_16, in_5, in_4, in_1, not_24_out, in_2);
  and and_12 (out_17, not_25_out, not_26_out, in_1, in_3, in_2);
  and and_13 (out_18, in_5, not_27_out, in_1, in_3, in_2);
  and and_14 (out_19, not_28_out, in_4, in_1, in_3, in_2);
  and and_15 (out_20, in_5, in_4, in_1, in_3, in_2);
endmodule

module Eixo_X_Unidades (
  input  [3:0] in_1,
  output G,
  output A,
  output B,
  output C,
  output D,
  output E,
  output F
);

  X_G x_g_1 (.out_2(G), .in_1(in_1));
  X_A u_A (.out_2(A), .in_1(in_1));
  X_B u_B (.out_2(B), .in_1(in_1));
  X_D x_d_1 (.out_2(D), .in_1(in_1));
  X_C x_c_1 (.out_2(C), .in_1(in_1));
  X_E u_E (.out_2(E), .in_1(in_1));
  X_F x_f_1 (.out_2(F), .in_1(in_1));
endmodule

module X_A (
  input  [3:0] in_1,
  output out_2
);

  wire and_1_out, and_2_out, and_3_out, and_4_out, and_5_out;

  and and_1 (and_1_out, ~in_1[3], ~in_1[1], in_1[0]);  // AND_Gate
  and and_2 (and_2_out, ~in_1[3], in_1[2], in_1[1]);  // AND_Gate
  or or_1 (out_2, and_1_out, and_2_out, and_4_out, and_3_out, and_5_out);
  and and_3 (and_3_out, in_1[3], ~in_1[2], in_1[0]);  // AND_Gate
  and and_4 (and_4_out, in_1[2], in_1[1], in_1[0]);
  and and_5 (and_5_out, in_1[3], ~in_1[2], in_1[1]);  // AND_Gate
endmodule

module X_B (
  input  [3:0] in_1,
  output out_2
);

  wire and_1_out, and_2_out, and_3_out, and_4_out, and_5_out, and_6_out;

  and and_1 (and_1_out, in_1[3], ~in_1[2]);  // AND_Gate
  and and_2 (and_2_out, in_1[3], in_1[1], ~in_1[0]);  // AND_Gate
  and and_3 (and_3_out, in_1[3], ~in_1[1], in_1[0]);  // AND_Gate
  or or_1 (out_2, and_1_out, and_3_out, and_2_out, and_4_out, and_6_out, and_5_out);
  and and_4 (and_4_out, ~in_1[3], in_1[2], ~in_1[0]);  // AND_Gate
  and and_5 (and_5_out, ~in_1[3], ~in_1[2], in_1[0]);  // AND_Gate
  and and_6 (and_6_out, ~in_1[3], in_1[1], in_1[0]);  // AND_Gate
endmodule

module X_C (
  input  [3:0] in_1,
  output out_2
);

  wire and_1_out, and_2_out, and_3_out;

  and and_1 (and_1_out, ~in_1[3], in_1[2], ~in_1[1]);  // AND_Gate
  or or_1 (out_2, in_1[3], and_1_out, and_2_out, and_3_out);
  and and_2 (and_2_out, ~in_1[3], ~in_1[1], in_1[0]);  // AND_Gate
  and and_3 (and_3_out, ~in_1[3], ~in_1[2], in_1[1]);  // AND_Gate
endmodule

module X_D (
  input  [3:0] in_1,
  output out_2
);

  wire and_1_out, and_2_out, and_3_out, and_4_out, and_5_out;

  and and_1 (and_1_out, in_1[3], ~in_1[2]);  // AND_Gate
  and and_2 (and_2_out, in_1[1], ~in_1[0]);  // AND_Gate
  or or_1 (out_2, and_1_out, and_2_out, and_3_out, and_4_out, and_5_out);
  and and_3 (and_3_out, in_1[2], in_1[1]);
  and and_4 (and_4_out, in_1[2], ~in_1[1], ~in_1[0]);  // AND_Gate
  and and_5 (and_5_out, ~in_1[3], ~in_1[1], in_1[0]);  // AND_Gate
endmodule

module X_E (
  input  [3:0] in_1,
  output out_2
);

  wire and_1_out, and_2_out, and_3_out, and_4_out, and_5_out, and_6_out;

  and and_1 (and_1_out, ~in_1[3], ~in_1[2], in_1[0]);  // AND_Gate
  and and_2 (and_2_out, ~in_1[3], in_1[1], in_1[0]);  // AND_Gate
  and and_3 (and_3_out, ~in_1[3], in_1[2], ~in_1[0]);  // AND_Gate
  or or_1 (out_2, and_1_out, and_2_out, and_3_out, and_4_out, and_5_out, and_6_out);
  and and_4 (and_4_out, in_1[2], in_1[1], ~in_1[0]);  // AND_Gate
  and and_5 (and_5_out, in_1[3], ~in_1[1], in_1[0]);  // AND_Gate
  and and_6 (and_6_out, in_1[3], ~in_1[2], in_1[0]);  // AND_Gate
endmodule

module X_F (
  input  [3:0] in_1,
  output out_2
);

  wire and_1_out, and_2_out, and_3_out, and_4_out;

  and and_1 (and_1_out, ~in_1[3], ~in_1[2], in_1[0]);  // AND_Gate
  and and_2 (and_2_out, ~in_1[3], in_1[1], in_1[0]);  // AND_Gate
  or or_1 (out_2, and_1_out, and_2_out, and_3_out, and_4_out);
  and and_3 (and_3_out, in_1[3], ~in_1[1], in_1[0]);  // AND_Gate
  and and_4 (and_4_out, in_1[3], ~in_1[2], in_1[0]);  // AND_Gate
endmodule

module X_G (
  input  [3:0] in_1,
  output out_2
);

  wire and_1_out, and_2_out, and_3_out, and_4_out, and_5_out, and_6_out;

  and and_1 (and_1_out, ~in_1[3], in_1[2]);  // AND_Gate
  and and_2 (and_2_out, in_1[2], in_1[1]);
  and and_3 (and_3_out, in_1[2], in_1[0]);
  or or_1 (out_2, and_1_out, and_3_out, and_2_out, and_4_out, and_5_out, and_6_out);
  and and_4 (and_4_out, ~in_1[3], in_1[1], in_1[0]);  // AND_Gate
  and and_5 (and_5_out, in_1[3], ~in_1[1], in_1[0]);  // AND_Gate
  and and_6 (and_6_out, in_1[3], in_1[1], ~in_1[0]);  // AND_Gate
endmodule

module Eixo_X_Dezenas (
  input  [3:0] in_1,
  output out_2,
  output out_3
);

  X0_Portas_A_B_E_e_F x0_portas_a_b_e_e_f_1 (.D(in_1[0]), .C(in_1[1]), .B(in_1[2]), .A(in_1[3]), .out_5(out_2));

  assign out_3 = 1'b1;
endmodule

module X0_Portas_A_B_E_e_F (
  input  D,
  input  C,
  input  B,
  input  A,
  output out_5
);

  wire and_1_out, and_2_out, and_3_out, and_4_out, and_5_out, not_1_out, not_2_out, not_3_out, not_4_out,
       not_5_out, not_6_out;

  not not_1 (not_1_out, A);
  not not_2 (not_2_out, A);
  not not_3 (not_3_out, A);
  not not_4 (not_4_out, B);
  not not_5 (not_5_out, B);
  not not_6 (not_6_out, D);
  and and_1 (and_1_out, not_1_out, C);
  and and_2 (and_2_out, not_2_out, D);
  and and_3 (and_3_out, not_3_out, B);
  and and_4 (and_4_out, A, not_4_out);
  and and_5 (and_5_out, not_5_out, C, not_6_out);
  or or_1 (out_5, and_1_out, and_2_out, and_3_out, and_4_out, and_5_out);
endmodule

module Eixo_Y_Unidades (
  input  [3:0] in_1,
  output G,
  output A,
  output B,
  output C,
  output D,
  output E,
  output F
);

  Y_G y_g_1 (.out_2(G), .in_1(in_1));
  Y_A y_a_1 (.out_2(A), .in_1(in_1));
  Y_B y_b_1 (.out_2(B), .in_1(in_1));
  Y_C y_c_1 (.out_2(C), .in_1(in_1));
  Y_D y_d_1 (.out_2(D), .in_1(in_1));
  Y_E y_e_1 (.out_2(E), .in_1(in_1));
  Y_F y_f_1 (.out_2(F), .in_1(in_1));
endmodule

module Y_A (
  input  [3:0] in_1,
  output out_2
);

  wire and_1_out, and_2_out, and_3_out, and_4_out, and_5_out;

  and and_1 (and_1_out, ~in_1[2], ~in_1[1], in_1[0]);  // AND_Gate
  and and_2 (and_2_out, ~in_1[3], in_1[2], ~in_1[1], in_1[0]);  // AND_Gate
  or or_1 (out_2, and_1_out, and_2_out, and_3_out, and_4_out, and_5_out);
  and and_3 (and_3_out, ~in_1[3], in_1[2], in_1[1]);  // AND_Gate
  and and_4 (and_4_out, in_1[3], in_1[2], in_1[1], in_1[0]);
  and and_5 (and_5_out, in_1[3], ~in_1[2], in_1[1]);  // AND_Gate
endmodule

module Y_B (
  input  [3:0] in_1,
  output out_2
);

  wire and_1_out, and_2_out, and_3_out, and_4_out;

  and and_1 (and_1_out, ~in_1[3], in_1[1]);  // AND_Gate
  and and_2 (and_2_out, in_1[2], in_1[0]);
  or or_1 (out_2, and_1_out, and_2_out, and_3_out, and_4_out);
  and and_3 (and_3_out, in_1[3], ~in_1[1]);  // AND_Gate
  and and_4 (and_4_out, ~in_1[2], in_1[1], ~in_1[0]);  // AND_Gate
endmodule

module Y_C (
  input  [3:0] in_1,
  output out_2
);

  wire and_1_out, and_2_out, and_3_out, and_4_out, and_5_out, and_6_out, and_7_out;

  and and_1 (and_1_out, ~in_1[3], in_1[2]);  // AND_Gate
  and and_2 (and_2_out, ~in_1[3], in_1[1]);  // AND_Gate
  and and_3 (and_3_out, in_1[3], in_1[2]);
  or or_1 (out_2, and_2_out, and_1_out, and_3_out, and_7_out, and_4_out, and_5_out, and_6_out);
  and and_4 (and_4_out, in_1[1], in_1[0]);
  and and_5 (and_5_out, ~in_1[3], ~in_1[1], in_1[0]);  // AND_Gate
  and and_6 (and_6_out, in_1[3], ~in_1[1], ~in_1[0]);  // AND_Gate
  and and_7 (and_7_out, in_1[3], in_1[1], in_1[0]);
endmodule

module Y_D (
  input  [3:0] in_1,
  output out_2
);

  wire and_1_out, and_2_out, and_3_out, and_4_out, and_5_out, and_6_out;

  and and_1 (and_1_out, in_1[1], ~in_1[0]);  // AND_Gate
  and and_2 (and_2_out, ~in_1[3], in_1[2]);  // AND_Gate
  and and_3 (and_3_out, in_1[2], in_1[1]);
  or or_1 (out_2, and_1_out, and_2_out, and_3_out, and_4_out, and_5_out, and_6_out);
  and and_4 (and_4_out, in_1[3], ~in_1[2]);  // AND_Gate
  and and_5 (and_5_out, ~in_1[3], ~in_1[1], in_1[0]);  // AND_Gate
  and and_6 (and_6_out, in_1[2], ~in_1[1], ~in_1[0]);  // AND_Gate
endmodule

module Y_E (
  input  [3:0] in_1,
  output out_2
);

  wire and_1_out, and_2_out, and_3_out, and_4_out, and_5_out;

  and and_1 (and_1_out, in_1[2], in_1[0]);
  and and_2 (and_2_out, ~in_1[3], ~in_1[2], in_1[1]);  // AND_Gate
  or or_1 (out_2, and_1_out, and_2_out, and_3_out, and_4_out, and_5_out);
  and and_3 (and_3_out, ~in_1[2], in_1[1], ~in_1[0]);  // AND_Gate
  and and_4 (and_4_out, in_1[3], in_1[2], ~in_1[1]);  // AND_Gate
  and and_5 (and_5_out, in_1[3], ~in_1[1], in_1[0]);  // AND_Gate
endmodule

module Y_F (
  input  [3:0] in_1,
  output out_2
);

  wire and_1_out, and_2_out, and_3_out;

  and and_1 (and_1_out, in_1[2], in_1[0]);
  or or_1 (out_2, and_1_out, and_3_out, and_2_out);
  and and_2 (and_2_out, ~in_1[3], in_1[1], in_1[0]);  // AND_Gate
  and and_3 (and_3_out, in_1[3], ~in_1[1], in_1[0]);  // AND_Gate
endmodule

module Y_G (
  input  [3:0] in_1,
  output out_2
);

  wire and_1_out, and_2_out, and_3_out, and_4_out, and_5_out;

  and and_1 (and_1_out, ~in_1[3], in_1[1]);  // AND_Gate
  and and_2 (and_2_out, in_1[3], ~in_1[2], in_1[1]);  // AND_Gate
  or or_1 (out_2, and_1_out, and_2_out, and_4_out, and_3_out, and_5_out);
  and and_3 (and_3_out, in_1[3], in_1[2], ~in_1[1]);  // AND_Gate
  and and_4 (and_4_out, in_1[3], ~in_1[1], in_1[0]);  // AND_Gate
  and and_5 (and_5_out, ~in_1[2], ~in_1[1], in_1[0]);  // AND_Gate
endmodule

module Eixo_Y_Dezenas (
  input  [3:0] in_1,
  output out_2,
  output out_3
);

  Y0_Portas_A_B_E_e_F y0_portas_a_b_e_e_f_1 (.D(in_1[0]), .C(in_1[1]), .B(in_1[2]), .A(in_1[3]), .out_5(out_2));

  assign out_3 = 1'b1;
endmodule

module Y0_Portas_A_B_E_e_F (
  input  D,
  input  C,
  input  B,
  input  A,
  output out_5
);

  wire and_1_out;

  and and_1 (and_1_out, B, C);
  or or_1 (out_5, and_1_out, A);
endmodule
